# Fritzing sketch RealFakeGarageDoors (saved by Fritzing 0.9.3b)
breadboards: 1

parts:
  R2 = Resistor [tolerance=±5% resistance=10k package=THT]
  U1 = NodeMCU V1.0
  R3 = Resistor [tolerance=±5% resistance=10k package=THT]
  Q2 = Basic FET P-Channel [part_number=BS250 package="TO220 [THT]"]
  Power_plug1 = Power plug
  Q1 = NPN-Transistor [part_number=PN2222 package="TO92 [THT]"]
  R1 = Resistor [tolerance=±5% resistance=680 package="0805 [SMD]"]
  R4 = Resistor [tolerance=±5% resistance=680 package="0805 [SMD]"]
  Q3 = NPN-Transistor [part_number=PN2222 package="TO92 [THT]"]
  Q4 = Basic FET P-Channel [part_number=BS250 package="TO220 [THT]"]
  R5 = Resistor [tolerance=±5% resistance=10k package=THT]
  R6 = Resistor [tolerance=±5% resistance=10k package=THT]
  U2 = mystery part, 3 pins [chip_label="Button 1" part_number="Remote Button 1"]
  U3 = mystery part, 1 pin [chip_label="Button 2" part_number="Remote Button 2"]

nets (from the schematic view):
  GND: R2.Pin_0, U1.GND, Power_plug1.GND, Q1.E, Q3.E, U2.pin3
  N1: R2.Pin_1, Q1.B, R1.Pin_1
  N2: U1.D1, R1.Pin_0
  N3: U1.D5, R4.Pin_0
  9V: U1.Vin, R3.Pin_1, Q2.source, Power_plug1.VCC, Q4.source, R5.Pin_1, U2.pin1
  N4: R3.Pin_0, Q2.gate, Q1.C
  N5: Q2.drain, U2.pin2
  N6: R4.Pin_1, Q3.B, R6.Pin_1
  N7: Q3.C, Q4.gate, R5.Pin_0
  N8: Q4.drain, U3.pin1

notes:
  Real Fake Garage Doors
  Remote Button 1
  Remote Button 2

custom parts:
  NodeMCU V1.0: ESP8266 based NodeMCU
